# Fritzing sketch arduino_esp8266_batteryshield_diagram (saved by Fritzing 0.9.10b)
breadboards: 1

parts:
  HC-SR04_Sensor_2 = HC-SR04 Ultrasonic Distance Sensor  # not connected
  WeMos_D1_Mini_Battery_Shield1 = WeMos D1 Mini Battery Shield
  A2 = WeMos D1 Mini (reversed pins)  # not connected
  WeMos_D1_Mini1 = WeMos D1 Mini
  BAT1 = Battery Holders [package=lipo-1100mAh]  # not connected
  U1 = LIPO-1000mAh [package=lipo-1000]  # not connected

nets:
  3V3: WeMos_D1_Mini_Battery_Shield1.3V3, WeMos_D1_Mini1.3V3
  5V: WeMos_D1_Mini_Battery_Shield1.5V, WeMos_D1_Mini1.5V
  N1: WeMos_D1_Mini_Battery_Shield1.D6, WeMos_D1_Mini1.D6
  N2: WeMos_D1_Mini_Battery_Shield1.D7, WeMos_D1_Mini1.D7
  N3: WeMos_D1_Mini_Battery_Shield1.G, WeMos_D1_Mini1.G

custom parts:
  WeMos D1 Mini (reversed pins): The D1 mini is a mini wifi board based on ESP-8266EX. (feb 2020 increase pcb hole sizes to 0.038 to accomadate .1 headers, change connectors from female to male, make connector id connector number rather than description) (May 2022 Reverse the pins (flip the board over so the pins are connected to the bottom of the board.)
