# Fritzing sketch arduino_esp8266_diagram (saved by Fritzing 0.9.10b)
breadboards: 1

parts:
  HC-SR04_Sensor_2 = HC-SR04 Ultrasonic Distance Sensor
  A1 = WeMos D1 Mini (reversed pins)
  BAT2 = Battery Holders [package=battery-aa-panel]
  BAT3 = Battery Holders [package=battery-aa-panel]

nets:
  VCC: HC-SR04_Sensor_2.VCC, A1.3V3
  N1: HC-SR04_Sensor_2.TRIG, A1.D7
  N2: HC-SR04_Sensor_2.ECHO, A1.D6
  N3: HC-SR04_Sensor_2.GND, A1.G, BAT2.-
  N4: A1.5V, BAT3.+
  N5: BAT2.+, BAT3.-

custom parts:
  WeMos D1 Mini (reversed pins): The D1 mini is a mini wifi board based on ESP-8266EX. (feb 2020 increase pcb hole sizes to 0.038 to accomadate .1 headers, change connectors from female to male, make connector id connector number rather than description) (May 2022 Reverse the pins (flip the board over so the pins are connected to the bottom of the board.)
